# Fritzing sketch Beat707 NXT V1-Arduino-Mini (saved by Fritzing 0.9.3b)
circuit board: 10cm x 4.9cm
breadboards: 2

parts:
  47uF = Electrolytic Capacitor [capacitance=1µF package="100 mil [THT, electrolytic]"]
  10k = Resistor [tolerance=±5% resistance=10k package=THT]
  MIDI_Output = MIDI_CONN_FEMALE_SUPPORT [part_number="MIDI Output" package=din_5_female_support]
  W25Q64 = IC, DIP package, 8 pins [chip_label=Flash part_number="W25Q64 (Winbond)"]
  Main_Header = male pin header, 7 pins [form="♂ (male)"]
  33 = Resistor [tolerance=±5% resistance=33 package=THT]
  4N35 = Optocoupler [package=THT]
  1N4748 = Rectifier Diode [part_number=1N4748 package="300 mil [THT]"]
  MIDI_Input = MIDI_CONN_FEMALE_SUPPORT [part_number="MIDI Input" package=din_5_female_support]
  1k = Resistor [tolerance=±5% resistance=1k package=THT]
  220 = Resistor [tolerance=±5% resistance=220 part_number=O1 package=THT]
  part = Ceramic Capacitor [capacitance=100nF package="100 mil [THT, multilayer]"]
  Bauteil1 = Arduino Pro Mini v13
  LD33V = LD33 Low-Dropout Voltage Regulator [part_number=LD33V]
  47uF2 = Electrolytic Capacitor [capacitance=1µF package="100 mil [THT, electrolytic]"]
  10 = Resistor [tolerance=±5% resistance=10 package=THT]

nets:
  GND: 47uF.-, MIDI_Output.NC1, W25Q64.pin4, Main_Header.pin2, 4N35.Pin_6, MIDI_Input.NC1, part.0, Bauteil1.GND, LD33V.GND, 47uF2.-
  N1: 47uF.+, 10k.Pin_1, W25Q64.pin3, W25Q64.pin7, W25Q64.pin8, part.1, Bauteil1.VCC, LD33V.Vout, 10.Pin_1
  N2: 10k.Pin_0, Bauteil1.RESET
  N3: MIDI_Output.MIDI_IN, 33.Pin_1
  N4: MIDI_Output.MIDI_OUT, 10.Pin_0
  N5: W25Q64.pin1, Bauteil1.D10_PWM/SS
  N6: W25Q64.pin2, Bauteil1.D12/MISO
  N7: W25Q64.pin5, Bauteil1.D11_PWM/MOSI
  N8: W25Q64.pin6, Bauteil1.D13/SCK
  N9: Main_Header.pin1, 1k.Pin_1, LD33V.Vin, 47uF2.+
  N10: Main_Header.pin3, Bauteil1.D8
  N11: Main_Header.pin4, Bauteil1.D9_PWM
  N12: Main_Header.pin5, Bauteil1.D5_PWM
  N13: Main_Header.pin6, Bauteil1.D6_PWM
  N14: Main_Header.pin7, Bauteil1.D7
  N15: 33.Pin_0, Bauteil1.D0/TX
  N16: 4N35.Pin_1, 1N4748.cathode, 220.Pin_0
  N17: 4N35.Pin_2, 1N4748.anode, MIDI_Input.MIDI_IN
  N18: 4N35.Pin_5, 1k.Pin_0, Bauteil1.D1/RX
  N19: MIDI_Input.MIDI_OUT, 220.Pin_1

notes:
  GND
  Beat707.com (c) 2017
  Wusik.com
  Kalfelz.com
  V1
  5V
  Beat707 NXT
  3.3V
  1uF
