# Fritzing sketch Beat707 NXT V1 (saved by Fritzing 0.9.3b)
circuit board: 10cm x 4.9cm
breadboards: 3

parts:
  47uF = Electrolytic Capacitor [capacitance=1µF package="100 mil [THT, electrolytic]"]
  AtMega328_3_3V_8Mhz = atmega328 [part_number=IC2 package=dip]
  10k = Resistor [tolerance=±5% resistance=10k package=THT]
  MIDI_Output = MIDI_CONN_FEMALE_SUPPORT [part_number="MIDI Output" package=din_5_female_support]
  10 = Resistor [tolerance=±5% resistance=10 package=THT]
  M_Out = female pin header, 2 pins [form="♀ (female)"]
  100nF = Ceramic Capacitor [capacitance=100nF package="100 mil [THT, multilayer]"]
  USB_5V = USB connector [package=THT]
  Power = female pin header, 2 pins [form="♀ (female)"]
  W25Q64 = IC, DIP package, 8 pins [chip_label=Flash part_number="W25Q64 (Winbond)"]
  FTDI = male pin header, 6 pins [form="♂ (male)"]
  Main_Header = male pin header, 7 pins [form="♂ (male)"]
  100nF_2 = Ceramic Capacitor [capacitance=100nF package="100 mil [THT, multilayer]"]
  33 = Resistor [tolerance=±5% resistance=33 package=THT]
  LD33V = LD33 Low-Dropout Voltage Regulator [part_number=LD33V]
  M_In = female pin header, 2 pins [form="♀ (female)"]
  4N35 = Optocoupler [package=THT]
  1N4748 = Rectifier Diode [part_number=1N4748 package="300 mil [THT]"]
  MIDI_Input = MIDI_CONN_FEMALE_SUPPORT [part_number="MIDI Input" package=din_5_female_support]
  1k = Resistor [tolerance=±5% resistance=1k package=THT]
  220 = Resistor [tolerance=±5% resistance=220 part_number=O1 package=THT]
  100nF_3 = Ceramic Capacitor [capacitance=100nF package="100 mil [THT, multilayer]"]
  part = Ceramic Capacitor [capacitance=100nF package="100 mil [THT, multilayer]"]
  A54 = male pin header, 2 pins [form="♂ (male)"]
  100nF_4 = Ceramic Capacitor [capacitance=100nF package="100 mil [THT, multilayer]"]
  100nF_5 = Ceramic Capacitor [capacitance=100nF package="100 mil [THT, multilayer]"]

nets:
  GND: 47uF.-, AtMega328_3_3V_8Mhz.GND, MIDI_Output.NC1, 100nF.0, USB_5V.GND, USB_5V.chassis5, W25Q64.pin4, FTDI.pin1, Main_Header.pin2, LD33V.GND, 4N35.Pin_4, 100nF_3.0, part.1, 100nF_4.0, 100nF_4.1, 100nF_5.0
  N1: 47uF.+, AtMega328_3_3V_8Mhz.VCC, AtMega328_3_3V_8Mhz.AVCC, AtMega328_3_3V_8Mhz.AREF, 10k.Pin_0, 10.Pin_1, 100nF.1, W25Q64.pin3, W25Q64.pin7, W25Q64.pin8, LD33V.Vout, 100nF_3.1, 100nF_5.1
  N2: AtMega328_3_3V_8Mhz.RESET, 10k.Pin_1, 100nF_2.1
  N3: AtMega328_3_3V_8Mhz.D0_(RX), FTDI.pin4, M_In.pin2
  N4: AtMega328_3_3V_8Mhz.D1_(TX), FTDI.pin5, 33.Pin_0
  N5: AtMega328_3_3V_8Mhz.D5_(PWM), Main_Header.pin5
  N6: AtMega328_3_3V_8Mhz.D6_(PWM), Main_Header.pin6
  N7: AtMega328_3_3V_8Mhz.D7, Main_Header.pin7
  N8: AtMega328_3_3V_8Mhz.D8, Main_Header.pin3
  N9: AtMega328_3_3V_8Mhz.D9_(PWM), Main_Header.pin4
  N10: AtMega328_3_3V_8Mhz.D10_(PWM), W25Q64.pin1
  N11: AtMega328_3_3V_8Mhz.D11_(PWM), W25Q64.pin5
  N12: AtMega328_3_3V_8Mhz.D12, W25Q64.pin2
  N13: AtMega328_3_3V_8Mhz.D13, W25Q64.pin6
  N14: AtMega328_3_3V_8Mhz.A4, A54.pin2
  N15: AtMega328_3_3V_8Mhz.A5, A54.pin1
  N16: MIDI_Output.MIDI_IN, M_Out.pin2
  N17: MIDI_Output.MIDI_OUT, 10.Pin_0
  N18: M_Out.pin1, 33.Pin_1
  N19: USB_5V.5V, Power.pin2
  N20: Power.pin1, FTDI.pin3, Main_Header.pin1, LD33V.Vin, 1k.Pin_1, part.0
  N21: FTDI.pin6, 100nF_2.0
  N22: M_In.pin1, 4N35.Pin_5, 1k.Pin_0
  N23: 4N35.Pin_1, 1N4748.cathode, 220.Pin_0
  N24: 4N35.Pin_2, 1N4748.anode, MIDI_Input.MIDI_IN
  N25: MIDI_Input.MIDI_OUT, 220.Pin_1

notes:
  GND
  Beat707.com (c) 2017
  Wusik.com
  Kalfelz.com
  V1
  5V
  Beat707 NXT
